# Fritzing sketch Schematics (saved by Fritzing 0.9.3b)

parts:
  M1 = DC Motor
  M2 = DC Motor
  U1 = L298 [package=multiwatt15]
  U2 = LIPO-2000mAh [package=lipo-2000]
  Part1 = Arduino Uno (Rev3)
  U3 = LIPO-2000mAh [package=lipo-2000]
  M3 = RioRand LM2596
  RE1 = Rotary Encoder [package=THT]
  RE2 = Rotary Encoder [package=THT]
  VCC1 = 4 x AAA Battery Mount

nets:
  N1: M1.pin_1, U1.OUT1
  N2: M1.pin_2, U1.OUT2
  N3: M2.pin_1, U1.OUT3
  N4: M2.pin_2, U1.OUT4
  N5: U1.VS, M3.Pin_3
  N6: U1.IN1, Part1.D2
  N7: U1.ENA, Part1.D10_PWM/SS
  N8: U1.IN2, Part1.D3_PWM
  N9: U1.GND, M3.Pin_4
  N10: U1.IN3, Part1.D4
  N11: U1.ENB, Part1.D11_PWM/MOSI
  N12: U1.IN4, Part1.D5_PWM
  N13: U2.+, U3.-
  N14: U2.-, M3.Pin_2
  N15: Part1.D8, RE2.EncoderPinB
  N16: Part1.D9_PWM, RE2.EncoderPinC
  N17: Part1.GND, VCC1.-
  N18: Part1.D6_PWM, RE1.EncoderPinB
  N19: Part1.D7, RE1.EncoderPinC
  N20: Part1.3V3, RE1.EncoderPinA, RE2.EncoderPinA
  N21: Part1.VIN, VCC1.+
  N22: U3.+, M3.Pin_1

notes:
  7.4V 2200mAh
  12V
